# Fritzing sketch MidiMassOrgel (saved by Fritzing 0.9.3b)
breadboards: 1
perfboards: 1

parts:
  Bauteil1 = Arduino Uno (Rev3)
  LED1 = smd LED [color="Red (633nm)" package="0805 [SMD]"]
  C1 = Electrolytic Capacitor [capacitance=1µF package="100 mil [THT, electrolytic]"]
  R1 = Resistor [tolerance=±5% resistance=220 package="2010 [SMD]"]
  J1 = Basic Servo
  J2 = Basic Servo
  J3 = Basic Servo
  J4 = Basic Servo
  J5 = Basic Servo
  J6 = Basic Servo
  J7 = Basic Servo
  J8 = female pin header, 4 pins [form="♀ (female)"]
  Power_plug1 = Power plug

nets:
  N1: Bauteil1.D8, J2.pulse
  N2: Bauteil1.D9_PWM, J4.pulse
  N3: Bauteil1.D10_PWM/SS, J5.pulse
  N4: Bauteil1.D11_PWM/MOSI, J6.pulse
  N5: Bauteil1.D12/MISO, J7.pulse
  N6: Bauteil1.D13/SCK, R1.Pin_0
  GND: Bauteil1.GND, LED1.anode, C1.-, J1.gnd, J2.gnd, J3.gnd, J4.gnd, J5.gnd, J6.gnd, J7.gnd, J8.pin4, Power_plug1.GND
  N7: Bauteil1.D2, J8.pin3
  N8: Bauteil1.D3_PWM, J8.pin2
  N9: Bauteil1.D6_PWM, J1.pulse
  N10: Bauteil1.D7, J3.pulse
  VCC: Bauteil1.VIN, C1.+, J1.vcc, J2.vcc, J3.vcc, J4.vcc, J5.vcc, J6.vcc, J7.vcc, J8.pin1, Power_plug1.VCC
  N11: LED1.cathode, R1.Pin_1

notes:
  MIDI Interface
